# Fritzing sketch uvclock (saved by Fritzing 0.9.3b)
breadboards: 1

parts:
  UV_LED_BL-L522VC = LED - 5mm [color="Blue (430nm)" package="5 mm [THT]"]
  470uf = Capacitor Polarized [package=cpol-radial-100uf-25v]
  2N2222 = NPN-Transistor [package="TO92 [THT]"]
  R3 = Resistor [tolerance=±5% resistance=1k package="2010 [SMD]"]
  Часть1 = Arduino Nano (Rev3.0)
  18650_UPS_5v = Lilypad Power Supply
  sg90 = Basic Servo
  sg90_2 = Basic Servo
  Sensor_button = TOUCH [package=touch1]
  DS1302 = Real Time Clock Module - DS1307 RTC Breakout Board
  R5 = Resistor [tolerance=±5% resistance=470 package="2010 [SMD]"]

nets:
  N1: UV_LED_BL-L522VC.cathode, 470uf.-, 2N2222.C, 18650_UPS_5v.GND, Sensor_button.T1
  N2: UV_LED_BL-L522VC.anode, Часть1.D12/MISO
  VCC: 470uf.+, 18650_UPS_5v.+, sg90.vcc, sg90_2.vcc, Sensor_button.T2, DS1302.5V
  GND: 2N2222.E, sg90.gnd, sg90_2.gnd, DS1302.GND
  N3: 2N2222.B, R3.Pin_1
  N4: R3.Pin_0, Часть1.D6
  N5: Часть1.D2, DS1302.SDA
  N6: Часть1.D3, R5.Pin_1
  N7: Часть1.D4, DS1302.SCL
  N8: Часть1.D5, DS1302.SQW
  N9: Часть1.D7, R5.Pin_0
  N10: Часть1.D9, sg90.pulse
  N11: Часть1.D10, sg90_2.pulse

notes:
  UV LED BL-L522VC
  405nm
